# Fritzing sketch lista_2.6 (saved by Fritzing 0.9.3b)
breadboards: 1

parts:
  Part1 = Arduino Uno (Rev3)
  S1 = Pushbutton [package="[THT]"]
  R1 = Resistor [tolerance=±5% resistance=10k package=THT]
  LED1 = RGB LED (com. cathode, rgb) [package="5 mm [THT]"]
  R3 = Resistor [tolerance=±5% resistance=220 package=THT]
  R4 = Resistor [tolerance=±5% resistance=220 package=THT]
  R5 = Resistor [tolerance=±5% resistance=220 package=THT]

nets:
  N1: Part1.D9_PWM, R4.Pin_1
  N2: Part1.D10_PWM/SS, R3.Pin_1
  N3: Part1.D11_PWM/MOSI, R5.Pin_1
  N4: Part1.D2, S1.Pin_1, S1.Pin_2, R1.Pin_0
  N5: Part1.5V, S1.Pin_3, S1.Pin_4
  N6: Part1.GND, R1.Pin_1, LED1.common_cathode
  N7: LED1.red_anode, R5.Pin_0
  N8: LED1.green_anode, R3.Pin_0
  N9: LED1.blue_anode, R4.Pin_0
